# Fritzing sketch pulsera (saved by Fritzing 1.0.1rc)
breadboards: 1

parts:
  esp1 = ESP32 DevKitc V4
  U1 = MLX90614 [package=to-39]
  M1 = MakerFocus MAX30102
  M3 = BME280
  OLED_I2C1 = OLED 128x64 I2C Monochrome Display
  M4 = gy9250
  TP1 = TP4056 [chip_label=TP4056 package="DIP (Dual Inline) [THT]"]
  U3 = LIPO-1000mAh [package=lipo-1000]
  S1 = SWITCH-MOMENTARY-2 [package=tactile-switch-1101ne]

nets:
  N1: esp1.IO21, U1.PWM_SDA, M1.SDA, M3.SCL, OLED_I2C1.SDA, M4.pin4
  N2: esp1.IO22, esp1.IO23, U1.SCL_VZ, M1.SCL, M3.SDA, OLED_I2C1.SCK, M4.pin3
  GND: esp1.GND, U1.VSS, M1.GND, M3.GND, OLED_I2C1.GND, M4.pin2, TP1.pin6
  VDD: esp1.3V3, U1.VDD, M1.VIN, OLED_I2C1.VDD, M4.pin1, S1.2
  N3: TP1.pin3, S1.1
  N4: TP1.pin4, U3.+
  N5: TP1.pin5, U3.-

custom parts:
  ESP32 DevKitc V4: ESP32-DevKitC board with ESP32-WROOM-32 module. ESP32-DevKitC V4 is a small-sized ESP32-based development board produced by Espressif. Most of the pins on the ESP module are broken out to the pin headers on the board. The pins D0, D1, D2, D3, CMD and CLK are used internally for communication between ESP32 and SPI flash memory. They are grouped on both sides near the USB connector. Avoid using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
  MakerFocus MAX30102: Oximeter module using the MAX30102 chip. As usual, if you want the mounting holes in pcb, you need to drag a hole over the pad in silkscreen to actually drill the hole (by default they are not drilled)
  BME280: Temperature Humidity Barometric presure Sensor
  gy9250: MPU-9250 module (three-axis gyroscope + three-axis acceleration + three-axis magnetic field). The generic model from ebay et. al. rather than the Sparkfun version.
  TP4056: A DIP stand-in part for whatever IC you want. With 6 pins on a 300mil dual inline package (DIP) footprint.
